# Fritzing sketch RFID Module with Antenna and Differential Driver (saved by Fritzing 0.7.11b)
breadboards: 1

parts:
  IC1 = IC, DIP package, 16 pins [chip_label=Drv part_number=75C1168]
  J1 = male pin header, 8 pins [form="♂ (male)"]
  IC2 = IC, DIP package, 24 pins [chip_label=RFID part_number="MicroRWD - IB Tech"]
  LED1 = LED - 5mm [color="Red (633nm)" package="5 mm [THT]"]
  R1 = Resistor [tolerance=±5% resistance=1k package=THT]
  LED2 = LED - 5mm [color="Green (560nm)" package="5 mm [THT]"]
  R2 = Resistor [tolerance=±5% resistance=1k package=THT]
  L1 = Inductor [package="400 mil [THT]"]
  L2 = Inductor [package="400 mil [THT]"]

nets:
  N1: IC1.pin1, J1.pin5
  N2: IC1.pin2, J1.pin4
  5V: IC1.pin4, IC1.pin12, IC1.pin16, J1.pin7, IC2.pin8, R1.Pin_0, R2.Pin_0
  GND: IC1.pin8, J1.pin8, IC2.pin7, IC2.pin13, L1.pin_1, L2.pin_0
  N3: IC1.pin9, IC2.pin24
  N4: IC1.pin10, J1.pin2
  N5: IC1.pin11, J1.pin1
  N6: IC1.pin13, J1.pin6
  N7: IC1.pin14, J1.pin3
  N8: IC1.pin15, IC2.pin23
  N9: IC2.pin1, LED1.cathode
  N10: IC2.pin2, LED2.cathode
  N11: IC2.pin9, L1.pin_0
  N12: IC2.pin12, L2.pin_1
  N13: LED1.anode, R1.Pin_1

notes:
  Pin1 - CTS**
  Pin2 - CTS *
  Pin3 - Rx**
  Pin4 - Tx**
  Pin5 - Tx*
  Pin6 - Rx*
  Pin7 - +5V
  Pin8 - GND
  RFID Door Lock, RFID MicroRWD Module Board, 1.0
